# Fritzing sketch Lager_Maker (saved by Fritzing 0.7.10b)
breadboards: 1

parts:
  Arduino1 = Arduino
  S1 = Pushbutton [package="[THT]"]
  J1 = Piezo Speaker
  Part2 = Sparkfun Relay Control PCB
  LED1 = Red LED - 5mm
  Relay1 = SPST N.O. Relay
  1K1 = Resistor [resistance=1k tolerance=±5% package=THT]
  1K2 = Resistor [resistance=1k tolerance=±5% package=THT]
  10K1 = Resistor [resistance=10k tolerance=±5% package=THT]
  Diode1 = Rectifier Diode [part_number=1N4001 package="300 mil [THT]"]
  NPN_Transistor1 = NPN-Transistor [package="TO92 [THT]"]
  R1 = Temperature Sensor (Thermistor) [thermistor_type=NTC package=THT]
  R2 = 10k Ω Resistor [package=THT]
  R3 = 10k Ω Resistor [package=THT]
  R4 = 330 Ω Resistor [package=THT]
  R5 = 10k Ω Resistor [package=THT]

nets:
  N1: Arduino1.GND, S1.Pin_3, S1.Pin_4, Part2.Ground, R3.Pin_1, R4.Pin_1
  N2: Arduino1.D13, Part2.Relay_Control
  N3: Arduino1.D9, J1.pin1
  N4: Arduino1.D2, S1.Pin_1, S1.Pin_2, R2.Pin_0
  N5: Arduino1.+5V, J1.pin2, Part2.Board_5V, R1.pin_0, R2.Pin_1, R5.Pin_1
  N6: Arduino1.A0, R1.pin_1, R3.Pin_0
  N7: Arduino1.A2, R4.Pin_0, R5.Pin_0
  N8: Part2.LED_Anode_(5V_in), LED1.anode
  N9: Part2.LED_Cathode, LED1.cathode
  N10: Part2.1K#5, 1K1.Pin_0
  N11: Part2.1K#6, 1K1.Pin_1
  N12: Part2.1N4148_Anode, Diode1.anode
  N13: Part2.1N4148_Cathode, Diode1.cathode
  N14: Part2.1K#9, 1K2.Pin_1
  N15: Part2.1K#10, 1K2.Pin_0
  N16: Part2.10K#11, 10K1.Pin_1
  N17: Part2.10K#12, 10K1.Pin_0
  N18: Part2.2N3904_Base, NPN_Transistor1.B
  N19: Part2.2N3904_Collector, NPN_Transistor1.C
  N20: Part2.2N3904_Emitter, NPN_Transistor1.E
  N21: Part2.Relay_Coil, Relay1.Coil/Gnd
  N22: Part2.Relay_5V, Relay1.5V
  N23: Part2.Relay_Load_1, Relay1.Load_1
  N24: Part2.Relay_Load_2, Relay1.Load_2

custom parts:
  Sparkfun Relay Control PCB: COM-09096
